# Fritzing sketch smartTemperatureMonitoring (saved by Fritzing 0.9.3b)
breadboards: 1

parts:
  Componente1 = Arduino Uno (Rev3) - ICSP
  S2 = Pushbutton [package="[SMD]"]
  Display1 = LCD screen 16x2 IIC [part_number=101290]
  J1 = Basic Servo
  R3 = Resistor [tolerance=±5% resistance=10k package="0603 [SMD]"]

nets:
  N1: Componente1.A4/SDA, Display1.SDA
  N2: Componente1.A5/SCL, Display1.SCL
  VCC: Componente1.5V, S2.Pin_1, S2.Pin_2, Display1.VCC, J1.vcc
  N3: Componente1.D9_PWM, J1.pulse
  GND: Componente1.GND, Display1.GND, J1.gnd, R3.Pin_0
  N4: Componente1.D5_PWM, S2.Pin_3, S2.Pin_4, R3.Pin_1

custom parts:
  LCD screen 16x2 IIC: LCD screen with HD44780 controller enables showing text, symbols, value or anything else that comes from Croduino/Arduino. It is capable of showing 16 symbols in two lines and therefore can be used in many projects that need to send clearly visible and legible output information.. • Color of symbols: White • Backlight: Blue • Dimensions: 80 x 36 x 12 mm • Screen dimensions: 64.5 x 16 mm •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
